# Fritzing sketch Platinenlayout (saved by Fritzing 0.9.10b)
breadboards: 1

parts:
  Bauteil1 = Arduino Nano 33 BLE Sense
  Bauteil2 = HX711 Weighing Sensor Module
  Load_Cell1 = Load Cell - Red/white/black/green
  R1 = Resistor [tolerance=±5% power=0.25 resistance=220 package=THT]
  R2 = Resistor [tolerance=±5% power=0.25 resistance=220 package=THT]
  R3 = Resistor [tolerance=±5% power=0.25 resistance=220 package=THT]
  LED1 = 7-SEGMENT-4DIGIT-YOUNGSUN [package=7-segment-4digit-youngsun]
  R4 = 1000 Ω Resistor [package=THT]

nets:
  N1: Bauteil1.D2, LED1.D
  N2: Bauteil1.D3~, LED1.DIG2
  N3: Bauteil1.D4, Bauteil2.CK/TX
  N4: Bauteil1.D5~, Bauteil2.DO/RX
  N5: Bauteil1.D6~, R1.Pin_1
  N6: Bauteil1.D7, R2.Pin_1
  N7: Bauteil1.D8, R3.Pin_1
  N8: Bauteil1.D9~, R4.Pin_0
  N9: Bauteil1.D10~, LED1.A
  N10: Bauteil1.D11/MOSI, Bauteil1.+5V, LED1.APOS-A
  N11: Bauteil1.D12~/MISO, LED1.E
  N12: Bauteil1.VIN, LED1.C
  GND: Bauteil1.GND, Bauteil1.A7, Bauteil2.GND
  N13: Bauteil1.A1, LED1.COL-A
  N14: Bauteil1.A0, LED1.DIG3
  3V3: Bauteil1.3V3, Bauteil2.VCC
  N15: Bauteil2.E+, Load_Cell1.wire1
  N16: Bauteil2.E-, Load_Cell1.wire3
  N17: Bauteil2.A+, Load_Cell1.wire2
  N18: Bauteil2.A-, Load_Cell1.wire4
  N19: R1.Pin_0, LED1.G
  N20: R2.Pin_0, LED1.COL-C
  N21: R3.Pin_0, LED1.F
  N22: LED1.DP, R4.Pin_1

custom parts:
  Arduino Nano 33 BLE Sense: The Nano 33 BLE Sense (without headers) is Arduino’s 3.3V AI enabled board in the smallest available form factor: 45x18mm! The Arduino Nano 33 BLE Sense is a completely new board on a well-known form factor. It comes with a series of embedded sensors: 9 axis inertial sensor: what makes this board ideal for wearable devices humidity, and temperature sensor: to get highly accurate measurements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
  Load Cell - Red/white/black/green: A rectangle load cell/weighting pressure Sensor with four wires - Red, white, black, green. Normally corresponding with E+, E-, A+, A- respectively.
  1000 Ω Resistor: A generic resistor (0.25W)
